# Fritzing sketch esp8266_sensors (saved by Fritzing 0.9.3b)
circuit board: 6.19267cm x 5.03818cm
perfboards: 1

parts:
  J2 = female pin header, 11 pins [form="♀ (female)"]
  R1 = Resistor [tolerance=±5% resistance=10k package=THT]
  IC1 = Voltage Regulator [package=to-92]
  DHT1 = DHT22_Humidity_and_Temperature_Sensor
  C3 = prefix0000
  C4 = prefix0000
  J6 = prefix0000
  S2 = Pushbutton [package="[THT]"]
  J1 = female pin header, 11 pins [form="♀ (female)"]
  J5 = male pin header, 2 pins [form="♂ (male)"]
  J4 = female pin header, 6 pins [form="♀ (female)"]
  U4 = mystery part, 5 pins [chip_label=?]
  U3 = mystery part, 5 pins [chip_label=?]
  U2 = mystery part, 5 pins [chip_label=?]
  U1 = mystery part, 5 pins [chip_label=?]
  U5 = mystery part, 5 pins [chip_label=?]
  J7 = male pin header, 4 pins [form="♂ (male)"]
  J8 = male pin header, 4 pins [form="♂ (male)"]
  J9 = male pin header, 4 pins [form="♂ (male)"]
  R2 = Resistor [tolerance=±5% resistance=10k package=THT]
  R3 = Resistor [tolerance=±5% resistance=10k package=THT]

nets:
  N1: J2.pin1, J7.pin2, J8.pin2, J9.pin2, R2.Pin_1
  N2: J2.pin5, R1.Pin_0, DHT1.connector2
  N3: J2.pin8, J5.pin1
  N4: J2.pin10, S2.Pin_3, S2.Pin_4, J5.pin2
  N5: R1.Pin_1, IC1.OUT, DHT1.connector1, C4.connector1, J1.pin1, J7.pin4, J8.pin4, J9.pin4, R2.Pin_0, R3.Pin_0
  N6: IC1.GND, DHT1.connector4, C3.connector0, C4.connector0, J6.connector0, S2.Pin_1, S2.Pin_2, J1.pin2, J4.pin1, J7.pin3, J8.pin3, J9.pin3
  N7: IC1.IN, C3.connector1, J6.connector1
  N8: J1.pin3, J4.pin5
  N9: J1.pin4, J4.pin4
  N10: J1.pin11, J7.pin1, J8.pin1, J9.pin1, R3.Pin_1
  N11: U4.pin1, U4.pin2, U4.pin3, U4.pin4, U4.pin5
  N12: U3.pin1, U3.pin2, U3.pin3, U3.pin4, U3.pin5
  N13: U2.pin1, U2.pin2, U2.pin3, U2.pin4, U2.pin5
  N14: U1.pin1, U1.pin2, U1.pin3, U1.pin4, U1.pin5
  N15: U5.pin1, U5.pin2, U5.pin3, U5.pin4, U5.pin5

notes:
  GND
  CTS
  POWER
  TXO
  RXI
  DTR
  GPIO1: U0TXD -> RXI
  GPIO3: U0RXD -> TXO
  RESET
  IC1: MCP1700-3302E/TO
  C1 and C2: 2.2µF
  Prototype Area
  3V3 GND SDA SCL
  I2C: GPIO4/22 -> SDA, GPIO5/11 -> SCL
